// Logisim project KMAPCircs.circ as structural Verilog: 5 circuits, main circuit main
module main (
  input  in_1,
  input  in_2,
  input  in_3,
  input  _8,
  input  _4,
  input  _2,
  input  _1,
  output out_8
);

  wire and_1_out, and_2_out, B_C_prime_out, B_D__prime_out, B_D_out, b_prime_out, BC_prime_out,
       BD__prime_out, BD_out, c_prime_out, d_prime_out, not_1_out, not_2_out, not_3_out;

  not not_1 (not_1_out, in_1);
  not not_2 (not_2_out, in_2);
  not not_3 (not_3_out, in_3);
  not b_prime (b_prime_out, _4);
  not c_prime (c_prime_out, _2);
  not d_prime (d_prime_out, _1);
  and and_1 (and_1_out, not_1_out, in_2);
  and and_2 (and_2_out, not_2_out, not_3_out);
  or or_1 (out_8, and_1_out, and_2_out);
  and BD (BD_out, _1, _4);
  not BD__prime (BD__prime_out, BD_out);
  // AND_Gate C_BD__prime has open pins: in0=BD__prime_out, in1=_2, out=open
  and BC_prime (BC_prime_out, c_prime_out, _4);
  // OR_Gate A__B_D__prime has open pins: in0=_8, in1=B_D__prime_out, out=open
  or B_C_prime (B_C_prime_out, c_prime_out, _4);
  // OR_Gate A_BC_prime has open pins: in0=_8, in1=BC_prime_out, out=open
  or B_D (B_D_out, _1, _4);
  not B_D__prime (B_D__prime_out, B_D_out);

  // Notes on the sheet:
  //   b'
  //   a
  //   b
  //   c'
  //   c
  //   d'
  //   d
  //   BD
  //   BC'
  //   B+C'
  //   B+D
endmodule

module BCDLED_1 (
  input  _8,
  input  _4,
  input  _2,
  input  _1,
  output _1_2,
  output _2_2,
  output _3,
  output _4_2,
  output _5
);

  wire and_1_out, and_2_out, and_3_out, and_4_out, and_5_out, and_6_out, and_8_out, and_9_out, b_prime_out,
       c_prime_out, d_prime_out, not_1_out, or_1_out;

  not b_prime (b_prime_out, _4);
  not c_prime (c_prime_out, _2);
  not d_prime (d_prime_out, _1);
  and and_1 (and_1_out, _4, _1);
  and and_2 (and_2_out, d_prime_out, b_prime_out);
  and and_3 (and_3_out, _4, _1);
  and and_4 (and_4_out, b_prime_out, d_prime_out);
  and and_5 (and_5_out, c_prime_out, d_prime_out);
  and and_6 (and_6_out, _1, _2);
  or or_1 (or_1_out, _2, b_prime_out);
  or or_2 (_1_2, _8, and_4_out, and_3_out, _2);
  or or_3 (_2_2, b_prime_out, and_5_out, and_6_out);
  or or_4 (_3, _4, c_prime_out, _1);
  and and_7 (_5, or_1_out, d_prime_out);
  not not_1 (not_1_out, and_1_out);
  and and_8 (and_8_out, and_1_out, c_prime_out);
  and and_9 (and_9_out, not_1_out, _2);
  or or_5 (_4_2, and_9_out, and_8_out, and_2_out, _8);
endmodule

module BCDLED_2 (
  input  _8,
  input  _4,
  input  _2,
  input  _1,
  output out_5,
  output out_6,
  output out_7,
  output out_8,
  output out_9,
  output out_10,
  output out_11,
  output _1_2,
  output out_13,
  output out_14,
  output out_15,
  output out_16,
  output out_17,
  output out_18,
  output _2_2,
  output _3,
  output _4_2,
  output _5,
  output _6,
  output _7
);

  wire A__B_D__prime_out, A_BC_prime_out, B_C_prime_out, B_D__prime_out, B_D_out, b_prime_out, BC_prime_out,
       BD__prime_out, BD_out, C_BD__prime_out, C_D_out, C_prime_BD_out, c_prime_out, CD_out, CD_prime_out,
       D_prime_B_C_prime_out, d_prime_out, not_1_out;

  not b_prime (b_prime_out, _4);
  not c_prime (c_prime_out, _2);
  not d_prime (d_prime_out, _1);
  and BD (BD_out, _1, _4);
  not BD__prime (BD__prime_out, BD_out);
  and BC_prime (BC_prime_out, c_prime_out, _4);
  and C_BD__prime (C_BD__prime_out, BD__prime_out, _2);
  or B_C_prime (B_C_prime_out, c_prime_out, _4);
  or A__B_D__prime (A__B_D__prime_out, _8, B_D__prime_out);
  or B_D (B_D_out, _1, _4);
  not B_D__prime (B_D__prime_out, B_D_out);
  or A_BC_prime (A_BC_prime_out, _8, BC_prime_out);
  _7_Segment_Display u_7_segment_display_1 (.g(_7), .f(_6), .a(_1_2), .b(_2_2), .e(_5), .d(_4_2), .c(_3));  // open: dp
  and CD (CD_out, _1, _2);
  or C_D (C_D_out, _1, _2);
  not not_1 (not_1_out, C_D_out);
  and C_prime_BD (C_prime_BD_out, BD_out, c_prime_out);
  and CD_prime (CD_prime_out, d_prime_out, c_prime_out);
  and D_prime_B_C_prime (D_prime_B_C_prime_out, B_C_prime_out, d_prime_out);
  or or_1 (_1_2, BD_out, A__B_D__prime_out, _2);
  or or_2 (_2_2, CD_out, b_prime_out, not_1_out);
  or or_3 (_3, B_C_prime_out, _1);
  or or_4 (_4_2, C_prime_BD_out, C_BD__prime_out, A__B_D__prime_out);
  or or_5 (_5, B_D__prime_out, CD_prime_out);
  or or_6 (_6, A_BC_prime_out, D_prime_B_C_prime_out);
  or or_7 (_7, A_BC_prime_out, C_BD__prime_out);

  assign out_5 = _1_2;
  assign out_6 = _2_2;
  assign out_7 = _3;
  assign out_8 = _4_2;
  assign out_9 = _5;
  assign out_10 = _6;
  assign out_11 = _7;
  assign out_13 = _2_2;
  assign out_14 = _3;
  assign out_15 = _4_2;
  assign out_16 = _5;
  assign out_17 = _6;
  assign out_18 = _7;

  // Notes on the sheet:
  //   a
  //   b'
  //   b
  //   d'
  //   c'
  //   c
  //   d
  //   (B_D)'
  //   BC'
  //   BD
  //   B+D
  //   B+C'
endmodule

module BCDLED_3 (
  input  _8,
  input  _4,
  input  _2,
  input  _1,
  output out_5,
  output out_6,
  output out_7,
  output out_8,
  output out_9,
  output out_10,
  output out_11
);

  wire B_prime_D_prime_out, b_prime_out, BC_prime_out, BD_out, BD_prime_out, C_prime_BD_out,
       C_prime_D_prime_out, c_prime_out, CB_prime_out, CD_out, CD_prime_out, d_prime_out;

  not b_prime (b_prime_out, _4);
  not c_prime (c_prime_out, _2);
  not d_prime (d_prime_out, _1);
  and B_prime_D_prime (B_prime_D_prime_out, d_prime_out, b_prime_out);
  and BD (BD_out, _1, _4);
  and C_prime_D_prime (C_prime_D_prime_out, d_prime_out, c_prime_out);
  and CD (CD_out, _1, _2);
  and CB_prime (CB_prime_out, _2, b_prime_out);
  and CD_prime (CD_prime_out, d_prime_out, _2);
  and C_prime_BD (C_prime_BD_out, _1, c_prime_out, _4);
  and BC_prime (BC_prime_out, c_prime_out, _4);
  and BD_prime (BD_prime_out, d_prime_out, _4);
  or or_1 (out_5, BD_out, B_prime_D_prime_out, _2, _8);
  or or_2 (out_6, CD_out, C_prime_D_prime_out, b_prime_out);
  or or_3 (out_7, _4, c_prime_out, _1);
  or or_4 (out_8, C_prime_BD_out, CD_prime_out, CB_prime_out, B_prime_D_prime_out, _8);
  or or_5 (out_9, CD_prime_out, B_prime_D_prime_out);
  or or_6 (out_10, BD_prime_out, BC_prime_out, C_prime_D_prime_out, _8);
  or or_7 (out_11, CD_prime_out, CB_prime_out, BC_prime_out, _8);
  _7_Segment_Display u_7_segment_display_1 (
    .g(out_11), .f(out_10), .a(out_5), .b(out_6), .e(out_9), .d(out_8), .c(out_7));  // open: dp

  // Notes on the sheet:
  //   D'
  //   D
  //   B
  //   C
  //   C'
  //   A
  //   B'
  //   B
  //   C'
  //   C
  //   D'
  //   D
  //   B'
  //   A
endmodule

module _5 (
  input  b,
  input  c,
  input  d,
  output out_4
);

  wire not_1_out, not_2_out, or_1_out;

  not not_1 (not_1_out, b);
  not not_2 (not_2_out, d);
  or or_1 (or_1_out, not_1_out, c);
  and and_1 (out_4, or_1_out, not_2_out);
endmodule
