// Logisim project 01 Gates.circ as structural Verilog: 12 circuits, main circuit Overview
module Overview (
  input  a,
  input  a_2,
  input  b,
  input  a_3,
  input  b_2,
  input  a_4,
  input  b_3,
  input  a_5,
  input  sel,
  input  b_4,
  input  In,
  input  Sel_2,
  input  [7:0] In_2,
  output a1,
  output a1_2,
  output a1_3,
  output a1_4,
  output out,
  output OutA,
  output OutA_2,
  output Out_2
);

  wire NAND_4_out, NAND_5_out, NAND_6_out, NAND_7_out, NAND_out, NOT_2_out, NOT_3_out, NOT_4_out, NOT_5_out,
       not_6_out, NOT_out, OR_2_out, OR_3_out, OR_4_out, OR_5_out, OR_6_out, OR_7_out;

  nand NAND (NAND_out, a_2, b);
  not NOT (NOT_out, a_3);
  not NOT_2 (NOT_2_out, b_2);
  not NOT_3 (NOT_3_out, a_4);
  not NOT_4 (NOT_4_out, b_3);
  not NOT_5 (NOT_5_out, sel);
  not not_6 (not_6_out, Sel_2);
  nand NAND_2 (a1, a, a);
  not not_7 (a1_2, NAND_out);
  nand NAND_3 (a1_3, NOT_out, NOT_2_out);
  and NAND_4 (NAND_4_out, NOT_3_out, b_3);
  and NAND_5 (NAND_5_out, a_4, NOT_4_out);
  nand NAND_6 (NAND_6_out, a_5, NOT_5_out);
  nand NAND_7 (NAND_7_out, sel, b_4);
  and AND (OutA, In, Sel_2);
  and AND_2 (OutA_2, not_6_out, In);
  or OR (a1_4, NAND_4_out, NAND_5_out);
  or OR_2 (OR_2_out, In_2[0], In_2[1]);
  or OR_3 (OR_3_out, In_2[2], In_2[3]);
  or OR_4 (OR_4_out, In_2[4], In_2[5]);
  or OR_5 (OR_5_out, In_2[6], In_2[7]);
  nand NAND_8 (out, NAND_6_out, NAND_7_out);
  or OR_6 (OR_6_out, OR_2_out, OR_3_out);
  or OR_7 (OR_7_out, OR_4_out, OR_5_out);
  or OR_8 (Out_2, OR_6_out, OR_7_out);

  // Notes on the sheet:
  //   Not from NAND
  //   AND from NOT and NAND
  //   OR from NOT and NAND
  //   XOR from NOT, OR, and NAND
  //   MUX from NAND
  //   DMUX from AND and NOT
  //   OR 8 way from OR
  //   SEE SIDEBAR FOR 16s AND OTHER CIRCUTS
endmodule

module NOT (
  input  a,
  output a1
);

  nand NAND (a1, a, a);

  // Notes on the sheet:
  //   Not from NAND
endmodule

module AND (
  input  a,
  input  b,
  output a1
);

  wire NAND_out;

  nand NAND (NAND_out, a, b);
  not NAND_2 (a1, NAND_out);

  // Notes on the sheet:
  //   AND from NOT and NAND
endmodule

module OR (
  input  a,
  input  b,
  output a1
);

  wire NOT_2_out, NOT_out;

  not NOT (NOT_out, a);
  not NOT_2 (NOT_2_out, b);
  nand NAND (a1, NOT_out, NOT_2_out);
endmodule

module XOR (
  input  a,
  input  b,
  output a1
);

  wire NAND_2_out, NAND_out, NOT_2_out, NOT_out;

  not NOT (NOT_out, a);
  not NOT_2 (NOT_2_out, b);
  and NAND (NAND_out, NOT_out, b);
  and NAND_2 (NAND_2_out, a, NOT_2_out);
  or OR (a1, NAND_out, NAND_2_out);
endmodule

module MUX (
  input  a,
  input  sel,
  input  b,
  output out
);

  wire NAND_2_out, NAND_out, NOT_out;

  not NOT (NOT_out, sel);
  nand NAND (NAND_out, a, NOT_out);
  nand NAND_2 (NAND_2_out, sel, b);
  nand NAND_3 (out, NAND_out, NAND_2_out);

  // Notes on the sheet:
  //   MUX from NAND
endmodule

module DMUX (
  input  In,
  input  Sel,
  output OutA,
  output OutB
);

  wire not_1_out;

  not not_1 (not_1_out, Sel);
  and AND (OutA, In, Sel);
  and AND_2 (OutB, not_1_out, In);

  // Notes on the sheet:
  //   DMUX from AND and NOT
endmodule

module NOT16 (
  input  [15:0] in_1,
  output [15:0] out_2
);

  not not_1 (out_2[0], in_1[0]);
  not not_2 (out_2[1], in_1[1]);
  not not_3 (out_2[2], in_1[2]);
  not not_4 (out_2[3], in_1[3]);
  not not_5 (out_2[4], in_1[4]);
  not not_6 (out_2[5], in_1[5]);
  not not_7 (out_2[6], in_1[6]);
  not not_8 (out_2[7], in_1[7]);
  not not_9 (out_2[8], in_1[8]);
  not not_10 (out_2[9], in_1[9]);
  not not_11 (out_2[10], in_1[10]);
  not not_12 (out_2[11], in_1[11]);
  not not_13 (out_2[12], in_1[12]);
  not not_14 (out_2[13], in_1[13]);
  not not_15 (out_2[14], in_1[14]);
  not not_16 (out_2[15], in_1[15]);
endmodule

module AND16 (
  input  [15:0] a,
  input  [15:0] b,
  output [15:0] Out
);

  and and_1 (Out[0], a[0], b[0]);
  and and_2 (Out[1], a[1], b[1]);
  and and_3 (Out[2], a[2], b[2]);
  and and_4 (Out[3], a[3], b[3]);
  and and_5 (Out[4], a[4], b[4]);
  and and_6 (Out[5], a[5], b[5]);
  and and_7 (Out[6], a[6], b[6]);
  and and_8 (Out[7], a[7], b[7]);
  and and_9 (Out[8], a[8], b[8]);
  and and_10 (Out[9], a[9], b[9]);
  and and_11 (Out[10], a[10], b[10]);
  and and_12 (Out[11], a[11], b[11]);
  and and_13 (Out[12], a[12], b[12]);
  and and_14 (Out[13], a[13], b[13]);
  and and_15 (Out[14], a[14], b[14]);
  and and_16 (Out[15], a[15], b[15]);
endmodule

module OR16 (
  input  [15:0] a,
  input  [15:0] b,
  output [15:0] Out
);

  or or_1 (Out[0], a[0], b[0]);
  or or_2 (Out[1], a[1], b[1]);
  or or_3 (Out[2], a[2], b[2]);
  or or_4 (Out[3], a[3], b[3]);
  or or_5 (Out[4], a[4], b[4]);
  or or_6 (Out[5], a[5], b[5]);
  or or_7 (Out[6], a[6], b[6]);
  or or_8 (Out[7], a[7], b[7]);
  or or_9 (Out[8], a[8], b[8]);
  or or_10 (Out[9], a[9], b[9]);
  or or_11 (Out[10], a[10], b[10]);
  or or_12 (Out[11], a[11], b[11]);
  or or_13 (Out[12], a[12], b[12]);
  or or_14 (Out[13], a[13], b[13]);
  or or_15 (Out[14], a[14], b[14]);
  or or_16 (Out[15], a[15], b[15]);
endmodule

module MUX16 (
  input  [15:0] a,
  input  Selector,
  input  [15:0] b,
  output [15:0] Out
);

  MUX mux_1 (.a(a[0]), .sel(Selector), .b(b[0]), .out(Out[0]));
  MUX mux_2 (.a(a[1]), .sel(Selector), .b(b[1]), .out(Out[1]));
  MUX mux_3 (.a(a[2]), .sel(Selector), .b(b[2]), .out(Out[2]));
  MUX mux_4 (.a(a[3]), .sel(Selector), .b(b[3]), .out(Out[3]));
  MUX mux_5 (.a(a[4]), .sel(Selector), .b(b[4]), .out(Out[4]));
  MUX mux_6 (.a(a[5]), .sel(Selector), .b(b[5]), .out(Out[5]));
  MUX mux_7 (.a(a[6]), .sel(Selector), .b(b[6]), .out(Out[6]));
  MUX mux_8 (.a(a[7]), .sel(Selector), .b(b[7]), .out(Out[7]));
  MUX mux_9 (.a(a[8]), .sel(Selector), .b(b[8]), .out(Out[8]));
  MUX mux_10 (.a(a[9]), .sel(Selector), .b(b[9]), .out(Out[9]));
  MUX mux_11 (.a(a[10]), .sel(Selector), .b(b[10]), .out(Out[10]));
  MUX mux_12 (.a(a[11]), .sel(Selector), .b(b[11]), .out(Out[11]));
  MUX mux_13 (.a(a[12]), .sel(Selector), .b(b[12]), .out(Out[12]));
  MUX mux_14 (.a(a[13]), .sel(Selector), .b(b[13]), .out(Out[13]));
  MUX mux_15 (.a(a[14]), .sel(Selector), .b(b[14]), .out(Out[14]));
  MUX mux_16 (.a(a[15]), .sel(Selector), .b(b[15]), .out(Out[15]));

  // Notes on the sheet:
  //   MUX
endmodule

module OR_8Way (
  input  [7:0] In,
  input  [7:0] In_2,
  output Out,
  output Out_2
);

  wire OR_2_out, OR_3_out, OR_4_out, OR_5_out, OR_6_out, OR_7_out;

  or OR (Out_2, In_2[0], In_2[1], In_2[2], In_2[3], In_2[4], In_2[5], In_2[6], In_2[7]);
  or OR_2 (OR_2_out, In[0], In[1]);
  or OR_3 (OR_3_out, In[2], In[3]);
  or OR_4 (OR_4_out, In[4], In[5]);
  or OR_5 (OR_5_out, In[6], In[7]);
  or OR_6 (OR_6_out, OR_2_out, OR_3_out);
  or OR_7 (OR_7_out, OR_4_out, OR_5_out);
  or OR_8 (Out, OR_6_out, OR_7_out);

  // Notes on the sheet:
  //   OR 8 way from OR
  //   OR 8 way from OR
endmodule
