// Logisim project 02.circ as structural Verilog
module HalfAdder (
  input  a,
  input  b,
  output sum,
  output carry
);

  xor Xor (sum, a, b);
  and And (carry, a, b);
endmodule

module FullAdder (
  input  a,
  input  b,
  input  c,
  output sum,
  output carry
);

  wire halfadder_1_carry, halfadder_1_sum, halfadder_2_carry;

  HalfAdder halfadder_1 (.a(a), .b(b), .sum(halfadder_1_sum), .carry(halfadder_1_carry));
  HalfAdder halfadder_2 (.a(halfadder_1_sum), .b(c), .sum(sum), .carry(halfadder_2_carry));
  HalfAdder halfadder_3 (.a(halfadder_1_carry), .b(halfadder_2_carry), .sum(carry));  // open: carry
endmodule

module Add16 (
  input  [15:0] a,
  input  [15:0] b,
  output [15:0] out_3
);

  wire fulladder_1_carry, fulladder_2_carry, fulladder_3_carry, fulladder_4_carry, fulladder_5_carry,
       fulladder_6_carry, fulladder_7_carry, fulladder_8_carry, fulladder_9_carry, fulladder_10_carry,
       fulladder_11_carry, fulladder_12_carry, fulladder_13_carry, fulladder_14_carry, halfadder_1_carry;

  HalfAdder halfadder_1 (.a(a[0]), .b(b[0]), .sum(out_3[0]), .carry(halfadder_1_carry));
  FullAdder fulladder_1 (.a(halfadder_1_carry), .b(a[1]), .c(b[1]), .sum(out_3[1]), .carry(fulladder_1_carry));
  FullAdder fulladder_2 (.a(fulladder_1_carry), .b(a[2]), .c(b[2]), .sum(out_3[2]), .carry(fulladder_2_carry));
  FullAdder fulladder_3 (.a(fulladder_2_carry), .b(a[3]), .c(b[3]), .sum(out_3[3]), .carry(fulladder_3_carry));
  FullAdder fulladder_4 (.a(fulladder_3_carry), .b(a[4]), .c(b[4]), .sum(out_3[4]), .carry(fulladder_4_carry));
  FullAdder fulladder_5 (.a(fulladder_4_carry), .b(a[5]), .c(b[5]), .sum(out_3[5]), .carry(fulladder_5_carry));
  FullAdder fulladder_6 (.a(fulladder_5_carry), .b(a[6]), .c(b[6]), .sum(out_3[6]), .carry(fulladder_6_carry));
  FullAdder fulladder_7 (.a(fulladder_6_carry), .b(a[7]), .c(b[7]), .sum(out_3[7]), .carry(fulladder_7_carry));
  FullAdder fulladder_8 (.a(fulladder_7_carry), .b(a[8]), .c(b[8]), .sum(out_3[8]), .carry(fulladder_8_carry));
  FullAdder fulladder_9 (.a(fulladder_8_carry), .b(a[9]), .c(b[9]), .sum(out_3[9]), .carry(fulladder_9_carry));
  FullAdder fulladder_10 (.a(fulladder_9_carry), .b(a[10]), .c(b[10]), .sum(out_3[10]), .carry(fulladder_10_carry));
  FullAdder fulladder_11 (.a(fulladder_10_carry), .b(a[11]), .c(b[11]), .sum(out_3[11]), .carry(fulladder_11_carry));
  FullAdder fulladder_12 (.a(fulladder_11_carry), .b(a[12]), .c(b[12]), .sum(out_3[12]), .carry(fulladder_12_carry));
  FullAdder fulladder_13 (.a(fulladder_12_carry), .b(a[13]), .c(b[13]), .sum(out_3[13]), .carry(fulladder_13_carry));
  FullAdder fulladder_14 (.a(fulladder_13_carry), .b(a[14]), .c(b[14]), .sum(out_3[14]), .carry(fulladder_14_carry));
  FullAdder fulladder_15 (.a(fulladder_14_carry), .b(a[15]), .c(b[15]), .sum(out_3[15]));  // open: carry
endmodule

module ALU (
  input  [15:0] x,
  input  [15:0] y,
  input  zx,
  input  zy,
  input  zx_2,
  input  zy_2,
  input  f,
  input  no,
  output [15:0] out,
  output zr,
  output ng
);

  wire or16foralu_1_out_2;
  wire [3:0] hexsplitter_1_out_2, hexsplitter_1_out_3, hexsplitter_1_out_4, hexsplitter_1_out_5;
  wire [15:0] add16_1_out_3, AND16_out, multiplexer_1_out, multiplexer_2_out, multiplexer_3_out,
       multiplexer_4_out, multiplexer_5_out, Not16_2_out, Not16_3_out, Not16_out;

  Multiplexer #(.width(16), .enable("false")) multiplexer_1 (
    .in0(x), .in1({16{1'b0}}), .out(multiplexer_1_out), .sel(zx));
  assign Not16_out = ~multiplexer_1_out;  // NOT_Gate Not16, 16 bits wide
  Multiplexer #(.width(16), .enable("false")) multiplexer_2 (
    .in0(y), .in1({16{1'b0}}), .out(multiplexer_2_out), .sel(zy));
  assign Not16_2_out = ~multiplexer_2_out;  // NOT_Gate Not16_2, 16 bits wide
  Multiplexer #(.width(16), .enable("false")) multiplexer_3 (
    .in0(multiplexer_1_out), .in1(Not16_out), .out(multiplexer_3_out), .sel(zx_2));
  Multiplexer #(.width(16), .enable("false")) multiplexer_4 (
    .in0(multiplexer_2_out), .in1(Not16_2_out), .out(multiplexer_4_out), .sel(zy_2));
  assign AND16_out = multiplexer_3_out & multiplexer_4_out;  // AND_Gate AND16, 16 bits wide
  Add16 add16_1 (.a(multiplexer_3_out), .b(multiplexer_4_out), .out_3(add16_1_out_3));
  LED led_1 (.in(f));
  Multiplexer #(.width(16), .enable("false")) multiplexer_5 (
    .in0(AND16_out), .in1(add16_1_out_3), .out(multiplexer_5_out), .sel(f));
  assign Not16_3_out = ~multiplexer_5_out;  // NOT_Gate Not16_3, 16 bits wide
  Multiplexer #(.width(16), .enable("false")) multiplexer_6 (
    .in0(multiplexer_5_out), .in1(Not16_3_out), .out({ng, out[14:0]}), .sel(no));
  OR16FORALU or16foralu_1 (.in_1({ng, out[14:0]}), .out_2(or16foralu_1_out_2));
  not not_1 (zr, or16foralu_1_out_2);
  Hex_Digit_Display hex_digit_display_1 (.value(hexsplitter_1_out_2));  // open: dp
  HexSplitter hexsplitter_1 (
    .in_1({ng, out[14:0]}), .out_2(hexsplitter_1_out_2), .out_3(hexsplitter_1_out_3),
    .out_4(hexsplitter_1_out_4), .out_5(hexsplitter_1_out_5));
  Hex_Digit_Display hex_digit_display_2 (.value(hexsplitter_1_out_3));  // open: dp
  Hex_Digit_Display hex_digit_display_3 (.value(hexsplitter_1_out_4));  // open: dp
  Hex_Digit_Display hex_digit_display_4 (.value(hexsplitter_1_out_5));  // open: dp

  assign out[15] = ng;

  // Notes on the sheet:
  //   ADD16
endmodule

module INC16 (
  input  [15:0] x,
  output [15:0] out_2
);

  Add16 add16_1 (.a(x), .b(16'h1), .out_3(out_2));
endmodule

module OR16FORALU (
  input  [15:0] in_1,
  output out_2
);

  wire or_1_out, or_2_out;

  or or_1 (or_1_out, in_1[13], in_1[4], in_1[15], in_1[14], in_1[12], in_1[11], in_1[10], in_1[9]);
  or or_2 (or_2_out, in_1[8], in_1[7], in_1[6], in_1[5], in_1[3], in_1[2], in_1[1], in_1[0]);
  or or_3 (out_2, or_1_out, or_2_out);
endmodule

module HexSplitter (
  input  [15:0] in_1,
  output [3:0] out_2,
  output [3:0] out_3,
  output [3:0] out_4,
  output [3:0] out_5
);


  assign out_2 = in_1[15:12];
  assign out_3 = in_1[11:8];
  assign out_4 = in_1[7:4];
  assign out_5 = in_1[3:0];
endmodule
