// Logisim project 3.circ as structural Verilog
module Bit (
  input  In,
  input  Load,
  output Out
);

  wire clock_1_out, multiplexer_1_out;

  Clock clock_1 (.out(clock_1_out));
  D_Flip_Flop d_ff_1 (.clk(clock_1_out), .D(multiplexer_1_out), .Q(Out));  // open: Qn, preset, en, reset
  Multiplexer #(.enable("false")) multiplexer_1 (.in0(Out), .in1(In), .out(multiplexer_1_out), .sel(Load));
endmodule

// reg
module Register (
  input  Load,
  input  [15:0] In,
  output [15:0] Out
);

  Bit bit_1 (.In(In[0]), .Load(Load), .Out(Out[0]));
  Bit bit_2 (.In(In[1]), .Load(Load), .Out(Out[1]));
  Bit bit_3 (.In(In[2]), .Load(Load), .Out(Out[2]));
  Bit bit_4 (.In(In[3]), .Load(Load), .Out(Out[3]));
  Bit bit_5 (.In(In[4]), .Load(Load), .Out(Out[4]));
  Bit bit_6 (.In(In[5]), .Load(Load), .Out(Out[5]));
  Bit bit_7 (.In(In[6]), .Load(Load), .Out(Out[6]));
  Bit bit_8 (.In(In[7]), .Load(Load), .Out(Out[7]));
  Bit bit_9 (.In(In[8]), .Load(Load), .Out(Out[8]));
  Bit bit_10 (.In(In[9]), .Load(Load), .Out(Out[9]));
  Bit bit_11 (.In(In[10]), .Load(Load), .Out(Out[10]));
  Bit bit_12 (.In(In[11]), .Load(Load), .Out(Out[11]));
  Bit bit_13 (.In(In[12]), .Load(Load), .Out(Out[12]));
  Bit bit_14 (.In(In[13]), .Load(Load), .Out(Out[13]));
  Bit bit_15 (.In(In[14]), .Load(Load), .Out(Out[14]));
  // Bit bit_16: pin names not known; wires that end beside it: Load, In[15], Load, Out[15]
endmodule

module RAM8 (
  input  [15:0] In,
  input  Load,
  input  [2:0] Address,
  output [15:0] Out
);

  wire demultiplexer_1_out0, demultiplexer_1_out1, demultiplexer_1_out2, demultiplexer_1_out3,
       demultiplexer_1_out4, demultiplexer_1_out5, demultiplexer_1_out6, demultiplexer_1_out7;
  wire [15:0] register_1_out, register_2_out, register_3_out, register_4_out, register_5_out, register_6_out,
       register_7_out, register_8_out;

  Demultiplexer #(.select(3), .enable("false")) demultiplexer_1 (
    .out0(demultiplexer_1_out0), .out1(demultiplexer_1_out1), .out2(demultiplexer_1_out2),
    .out3(demultiplexer_1_out3), .out4(demultiplexer_1_out4), .out5(demultiplexer_1_out5),
    .out6(demultiplexer_1_out6), .out7(demultiplexer_1_out7), .sel(Address));  // open: in
  Register register_1 (.In(In), .Load(demultiplexer_1_out0), .Out(register_1_out));
  Register register_2 (.In(In), .Load(demultiplexer_1_out1), .Out(register_2_out));
  Register register_3 (.In(In), .Load(demultiplexer_1_out2), .Out(register_3_out));
  Register register_4 (.In(In), .Load(demultiplexer_1_out3), .Out(register_4_out));
  Register register_5 (.In(In), .Load(demultiplexer_1_out4), .Out(register_5_out));
  Register register_6 (.In(In), .Load(demultiplexer_1_out5), .Out(register_6_out));
  Register register_7 (.In(In), .Load(demultiplexer_1_out6), .Out(register_7_out));
  Register register_8 (.In(In), .Load(demultiplexer_1_out7), .Out(register_8_out));
  Multiplexer #(.select(3), .width(16), .enable("false")) multiplexer_1 (
    .in0(register_1_out), .in1(register_2_out), .in2(register_3_out), .in3(register_4_out),
    .in4(register_5_out), .in5(register_6_out), .in6(register_7_out), .in7(register_8_out), .out(Out),
    .sel(Address));
endmodule

module RAM64 (
  input  [15:0] In,
  input  Load,
  input  [5:0] Address,
  output [15:0] Out
);

  wire demultiplexer_1_out0, demultiplexer_1_out1, demultiplexer_1_out2, demultiplexer_1_out3,
       demultiplexer_1_out4, demultiplexer_1_out5, demultiplexer_1_out6, demultiplexer_1_out7;
  wire [15:0] ram8_1_out, ram8_2_out, ram8_3_out, ram8_4_out, ram8_5_out, ram8_6_out, ram8_7_out, ram8_8_out;

  Demultiplexer #(.select(3), .enable("false")) demultiplexer_1 (
    .out0(demultiplexer_1_out0), .out1(demultiplexer_1_out1), .out2(demultiplexer_1_out2),
    .out3(demultiplexer_1_out3), .out4(demultiplexer_1_out4), .out5(demultiplexer_1_out5),
    .out6(demultiplexer_1_out6), .out7(demultiplexer_1_out7), .in(Load), .sel(Address[5:3]));
  RAM8 ram8_1 (.In(In), .Load(demultiplexer_1_out0), .Address(Address[2:0]), .Out(ram8_1_out));
  RAM8 ram8_2 (.In(In), .Load(demultiplexer_1_out1), .Address(Address[2:0]), .Out(ram8_2_out));
  RAM8 ram8_3 (.In(In), .Load(demultiplexer_1_out2), .Address(Address[2:0]), .Out(ram8_3_out));
  RAM8 ram8_4 (.In(In), .Load(demultiplexer_1_out3), .Address(Address[2:0]), .Out(ram8_4_out));
  RAM8 ram8_5 (.In(In), .Load(demultiplexer_1_out4), .Address(Address[2:0]), .Out(ram8_5_out));
  RAM8 ram8_6 (.In(In), .Load(demultiplexer_1_out5), .Address(Address[2:0]), .Out(ram8_6_out));
  RAM8 ram8_7 (.In(In), .Load(demultiplexer_1_out6), .Address(Address[2:0]), .Out(ram8_7_out));
  RAM8 ram8_8 (.In(In), .Load(demultiplexer_1_out7), .Address(Address[2:0]), .Out(ram8_8_out));
  Multiplexer #(.select(3), .width(16), .enable("false")) multiplexer_1 (
    .in0(ram8_1_out), .in1(ram8_2_out), .in2(ram8_3_out), .in3(ram8_4_out), .in4(ram8_5_out),
    .in5(ram8_6_out), .in6(ram8_7_out), .in7(ram8_8_out), .out(Out), .sel(Address[5:3]));
endmodule

module RAM512 (
  input  [15:0] In,
  input  Load,
  input  [8:0] Address,
  output [15:0] Out
);

  wire clock_1_out, demultiplexer_1_out0, demultiplexer_1_out1, demultiplexer_1_out2, demultiplexer_1_out3,
       demultiplexer_1_out4, demultiplexer_1_out5, demultiplexer_1_out6, demultiplexer_1_out7;
  wire [15:0] ram_1_data, ram_2_data, ram_3_data, ram_4_data, ram_5_data, ram_6_data, ram_7_data, ram_8_data;

  Demultiplexer #(.select(3), .enable("false")) demultiplexer_1 (
    .out0(demultiplexer_1_out0), .out1(demultiplexer_1_out1), .out2(demultiplexer_1_out2),
    .out3(demultiplexer_1_out3), .out4(demultiplexer_1_out4), .out5(demultiplexer_1_out5),
    .out6(demultiplexer_1_out6), .out7(demultiplexer_1_out7), .in(Load), .sel(Address[2:0]));
  Clock clock_1 (.out(clock_1_out));
  RAM #(.addrWidth(6), .dataWidth(16), .bus("separate")) ram_1 (
    .addr(Address[8:3]), .din(In), .data(ram_1_data), .str(demultiplexer_1_out0), .clk(clock_1_out));  // open: sel, ld, clr
  RAM #(.addrWidth(6), .dataWidth(16), .bus("separate")) ram_2 (
    .addr(Address[8:3]), .din(In), .data(ram_2_data), .str(demultiplexer_1_out1), .clk(clock_1_out));  // open: sel, ld, clr
  RAM #(.addrWidth(6), .dataWidth(16), .bus("separate")) ram_3 (
    .addr(Address[8:3]), .din(In), .data(ram_3_data), .str(demultiplexer_1_out2), .clk(clock_1_out));  // open: sel, ld, clr
  RAM #(.addrWidth(6), .dataWidth(16), .bus("separate")) ram_4 (
    .addr(Address[8:3]), .din(In), .data(ram_4_data), .str(demultiplexer_1_out3), .clk(clock_1_out));  // open: sel, ld, clr
  RAM #(.addrWidth(6), .dataWidth(16), .bus("separate")) ram_5 (
    .addr(Address[8:3]), .din(In), .data(ram_5_data), .str(demultiplexer_1_out4), .clk(clock_1_out));  // open: sel, ld, clr
  RAM #(.addrWidth(6), .dataWidth(16), .bus("separate")) ram_6 (
    .addr(Address[8:3]), .din(In), .data(ram_6_data), .str(demultiplexer_1_out5), .clk(clock_1_out));  // open: sel, ld, clr
  RAM #(.addrWidth(6), .dataWidth(16), .bus("separate")) ram_7 (
    .addr(Address[8:3]), .din(In), .data(ram_7_data), .str(demultiplexer_1_out6), .clk(clock_1_out));  // open: sel, ld, clr
  RAM #(.addrWidth(6), .dataWidth(16), .bus("separate")) ram_8 (
    .addr(Address[8:3]), .din(In), .data(ram_8_data), .str(demultiplexer_1_out7), .clk(clock_1_out));  // open: sel, ld, clr
  Multiplexer #(.select(3), .width(16), .enable("false")) multiplexer_1 (
    .in0(ram_1_data), .in1(ram_2_data), .in2(ram_3_data), .in3(ram_4_data), .in4(ram_5_data),
    .in5(ram_6_data), .in6(ram_7_data), .in7(ram_8_data), .out(Out), .sel(Address[2:0]));
endmodule

module RAM4K (
  input  [15:0] In,
  input  Load,
  input  [11:0] Address,
  output [15:0] Out
);

  wire clock_1_out, demultiplexer_1_out0, demultiplexer_1_out1, demultiplexer_1_out2, demultiplexer_1_out3,
       demultiplexer_1_out4, demultiplexer_1_out5, demultiplexer_1_out6, demultiplexer_1_out7;
  wire [15:0] ram_1_data, ram_2_data, ram_3_data, ram_4_data, ram_5_data, ram_6_data, ram_7_data, ram_8_data;

  Demultiplexer #(.select(3), .enable("false")) demultiplexer_1 (
    .out0(demultiplexer_1_out0), .out1(demultiplexer_1_out1), .out2(demultiplexer_1_out2),
    .out3(demultiplexer_1_out3), .out4(demultiplexer_1_out4), .out5(demultiplexer_1_out5),
    .out6(demultiplexer_1_out6), .out7(demultiplexer_1_out7), .in(Load), .sel(Address[2:0]));
  Clock clock_1 (.out(clock_1_out));
  RAM #(.addrWidth(9), .dataWidth(16), .bus("separate")) ram_1 (
    .addr(Address[11:3]), .din(In), .data(ram_1_data), .str(demultiplexer_1_out0), .clk(clock_1_out));  // open: sel, ld, clr
  RAM #(.addrWidth(9), .dataWidth(16), .bus("separate")) ram_2 (
    .addr(Address[11:3]), .din(In), .data(ram_2_data), .str(demultiplexer_1_out1), .clk(clock_1_out));  // open: sel, ld, clr
  RAM #(.addrWidth(9), .dataWidth(16), .bus("separate")) ram_3 (
    .addr(Address[11:3]), .din(In), .data(ram_3_data), .str(demultiplexer_1_out2), .clk(clock_1_out));  // open: sel, ld, clr
  RAM #(.addrWidth(9), .dataWidth(16), .bus("separate")) ram_4 (
    .addr(Address[11:3]), .din(In), .data(ram_4_data), .str(demultiplexer_1_out3), .clk(clock_1_out));  // open: sel, ld, clr
  RAM #(.addrWidth(9), .dataWidth(16), .bus("separate")) ram_5 (
    .addr(Address[11:3]), .din(In), .data(ram_5_data), .str(demultiplexer_1_out4), .clk(clock_1_out));  // open: sel, ld, clr
  RAM #(.addrWidth(9), .dataWidth(16), .bus("separate")) ram_6 (
    .addr(Address[11:3]), .din(In), .data(ram_6_data), .str(demultiplexer_1_out5), .clk(clock_1_out));  // open: sel, ld, clr
  RAM #(.addrWidth(9), .dataWidth(16), .bus("separate")) ram_7 (
    .addr(Address[11:3]), .din(In), .data(ram_7_data), .str(demultiplexer_1_out6), .clk(clock_1_out));  // open: sel, ld, clr
  RAM #(.addrWidth(9), .dataWidth(16), .bus("separate")) ram_8 (
    .addr(Address[11:3]), .din(In), .data(ram_8_data), .str(demultiplexer_1_out7), .clk(clock_1_out));  // open: sel, ld, clr
  Multiplexer #(.select(3), .width(16), .enable("false")) multiplexer_1 (
    .in0(ram_1_data), .in1(ram_2_data), .in2(ram_3_data), .in3(ram_4_data), .in4(ram_5_data),
    .in5(ram_6_data), .in6(ram_7_data), .in7(ram_8_data), .out(Out), .sel(Address[2:0]));
endmodule

module RAM16K (
  input  [15:0] In,
  input  Load,
  input  [13:0] Address,
  output [15:0] Out
);

  wire clock_1_out, demultiplexer_1_out0, demultiplexer_1_out1, demultiplexer_1_out2, demultiplexer_1_out3;
  wire [15:0] ram_1_data, ram_2_data, ram_3_data, ram_4_data;

  Demultiplexer #(.select(2), .enable("false")) demultiplexer_1 (
    .out0(demultiplexer_1_out0), .out1(demultiplexer_1_out1), .out2(demultiplexer_1_out2),
    .out3(demultiplexer_1_out3), .in(Load), .sel(Address[1:0]));
  Clock clock_1 (.out(clock_1_out));
  RAM #(.addrWidth(12), .dataWidth(16), .bus("separate")) ram_1 (
    .addr(Address[13:2]), .din(In), .data(ram_1_data), .str(demultiplexer_1_out0), .clk(clock_1_out));  // open: sel, ld, clr
  RAM #(.addrWidth(12), .dataWidth(16), .bus("separate")) ram_2 (
    .addr(Address[13:2]), .din(In), .data(ram_2_data), .str(demultiplexer_1_out1), .clk(clock_1_out));  // open: sel, ld, clr
  RAM #(.addrWidth(12), .dataWidth(16), .bus("separate")) ram_3 (
    .addr(Address[13:2]), .din(In), .data(ram_3_data), .str(demultiplexer_1_out2), .clk(clock_1_out));  // open: sel, ld, clr
  RAM #(.addrWidth(12), .dataWidth(16), .bus("separate")) ram_4 (
    .addr(Address[13:2]), .din(In), .data(ram_4_data), .str(demultiplexer_1_out3), .clk(clock_1_out));  // open: sel, ld, clr
  Multiplexer #(.select(2), .width(16), .enable("false")) multiplexer_1 (
    .in0(ram_1_data), .in1(ram_2_data), .in2(ram_3_data), .in3(ram_4_data), .out(Out), .sel(Address[1:0]));
endmodule

module PC (
  input  inc,
  input  [15:0] in,
  input  load,
  input  reset,
  output [15:0] out
);

  wire [15:0] adder_1_out, multiplexer_1_out, multiplexer_2_out, multiplexer_3_out;

  Multiplexer #(.width(16), .enable("false")) multiplexer_1 (
    .in0(out), .in1(adder_1_out), .out(multiplexer_1_out), .sel(inc));
  Multiplexer #(.width(16), .enable("false")) multiplexer_2 (
    .in0(multiplexer_1_out), .in1(in), .out(multiplexer_2_out), .sel(load));
  Multiplexer #(.width(16), .enable("false")) multiplexer_3 (
    .in0(multiplexer_2_out), .in1({16{1'b0}}), .out(multiplexer_3_out), .sel(reset));
  Adder #(.width(16)) adder_1 (.a(out), .b(16'h1), .out(adder_1_out));  // open: cin, cout
  Register register_1 (.In(multiplexer_3_out), .Load(1'b1), .Out(out));
endmodule
