// Logisim project Chapter 5.circ as structural Verilog
module Bit (
  input  In,
  input  Load,
  output Out
);

  wire clock_1_out, multiplexer_1_out;

  Clock clock_1 (.out(clock_1_out));
  D_Flip_Flop d_ff_1 (.clk(clock_1_out), .D(multiplexer_1_out), .Q(Out));  // open: Qn, preset, en, reset
  Multiplexer #(.enable("false")) multiplexer_1 (.in0(Out), .in1(In), .out(multiplexer_1_out), .sel(Load));
endmodule

module ALU (
  input  [15:0] x,
  input  [15:0] y,
  input  zx,
  input  zy,
  input  zx_2,
  input  zy_2,
  input  f,
  input  no,
  output [15:0] out,
  output zr,
  output ng
);

  wire fulladder_1_carry, fulladder_2_carry, fulladder_3_carry, fulladder_4_carry, fulladder_5_carry,
       fulladder_6_carry, fulladder_7_carry, fulladder_8_carry, fulladder_9_carry, fulladder_10_carry,
       fulladder_11_carry, fulladder_12_carry, fulladder_13_carry, fulladder_14_carry, halfadder_1_carry,
       or_1_out, or_3_out;
  wire [15:0] AND16_out, halfadder_1_sum, multiplexer_1_out, multiplexer_2_out, multiplexer_3_out,
       multiplexer_4_out, multiplexer_5_out, Not16_2_out, Not16_3_out, Not16_out;

  Multiplexer #(.width(16), .enable("false")) multiplexer_1 (
    .in0(x), .in1({16{1'b0}}), .out(multiplexer_1_out), .sel(zx));
  assign Not16_out = ~multiplexer_1_out;  // NOT_Gate Not16, 16 bits wide
  Multiplexer #(.width(16), .enable("false")) multiplexer_2 (
    .in0(y), .in1({16{1'b0}}), .out(multiplexer_2_out), .sel(zy));
  assign Not16_2_out = ~multiplexer_2_out;  // NOT_Gate Not16_2, 16 bits wide
  HalfAdder halfadder_1 (
    .a(multiplexer_3_out[0]), .b(multiplexer_4_out[0]), .sum(halfadder_1_sum[0]), .carry(halfadder_1_carry));
  Multiplexer #(.width(16), .enable("false")) multiplexer_3 (
    .in0(multiplexer_1_out), .in1(Not16_out), .out(multiplexer_3_out), .sel(zx_2));
  Multiplexer #(.width(16), .enable("false")) multiplexer_4 (
    .in0(multiplexer_2_out), .in1(Not16_2_out), .out(multiplexer_4_out), .sel(zy_2));
  FullAdder fulladder_1 (
    .a(halfadder_1_carry), .b(multiplexer_3_out[1]), .c(multiplexer_4_out[1]), .sum(halfadder_1_sum[1]),
    .carry(fulladder_1_carry));
  assign AND16_out = multiplexer_3_out & multiplexer_4_out;  // AND_Gate AND16, 16 bits wide
  FullAdder fulladder_2 (
    .a(fulladder_1_carry), .b(multiplexer_3_out[2]), .c(multiplexer_4_out[2]), .sum(halfadder_1_sum[2]),
    .carry(fulladder_2_carry));
  FullAdder fulladder_3 (
    .a(fulladder_2_carry), .b(multiplexer_3_out[3]), .c(multiplexer_4_out[3]), .sum(halfadder_1_sum[3]),
    .carry(fulladder_3_carry));
  LED led_1 (.in(f));
  Multiplexer #(.width(16), .enable("false")) multiplexer_5 (
    .in0(AND16_out), .in1(halfadder_1_sum), .out(multiplexer_5_out), .sel(f));
  assign Not16_3_out = ~multiplexer_5_out;  // NOT_Gate Not16_3, 16 bits wide
  FullAdder fulladder_4 (
    .a(fulladder_3_carry), .b(multiplexer_3_out[4]), .c(multiplexer_4_out[4]), .sum(halfadder_1_sum[4]),
    .carry(fulladder_4_carry));
  FullAdder fulladder_5 (
    .a(fulladder_4_carry), .b(multiplexer_3_out[5]), .c(multiplexer_4_out[5]), .sum(halfadder_1_sum[5]),
    .carry(fulladder_5_carry));
  Multiplexer #(.width(16), .enable("false")) multiplexer_6 (
    .in0(multiplexer_5_out), .in1(Not16_3_out), .out({ng, out[14:0]}), .sel(no));
  FullAdder fulladder_6 (
    .a(fulladder_5_carry), .b(multiplexer_3_out[6]), .c(multiplexer_4_out[6]), .sum(halfadder_1_sum[6]),
    .carry(fulladder_6_carry));
  or or_1 (or_1_out, out[13], out[4], ng, out[14], out[12], out[11], out[10], out[9]);
  or or_2 (zr, or_1_out, or_3_out);
  FullAdder fulladder_7 (
    .a(fulladder_6_carry), .b(multiplexer_3_out[7]), .c(multiplexer_4_out[7]), .sum(halfadder_1_sum[7]),
    .carry(fulladder_7_carry));
  FullAdder fulladder_8 (
    .a(fulladder_7_carry), .b(multiplexer_3_out[8]), .c(multiplexer_4_out[8]), .sum(halfadder_1_sum[8]),
    .carry(fulladder_8_carry));
  or or_3 (or_3_out, out[8], out[7], out[6], out[5], out[3], out[2], out[1], out[0]);
  FullAdder fulladder_9 (
    .a(fulladder_8_carry), .b(multiplexer_3_out[9]), .c(multiplexer_4_out[9]), .sum(halfadder_1_sum[9]),
    .carry(fulladder_9_carry));
  FullAdder fulladder_10 (
    .a(fulladder_9_carry), .b(multiplexer_3_out[10]), .c(multiplexer_4_out[10]), .sum(halfadder_1_sum[10]),
    .carry(fulladder_10_carry));
  FullAdder fulladder_11 (
    .a(fulladder_10_carry), .b(multiplexer_3_out[11]), .c(multiplexer_4_out[11]), .sum(halfadder_1_sum[11]),
    .carry(fulladder_11_carry));
  FullAdder fulladder_12 (
    .a(fulladder_11_carry), .b(multiplexer_3_out[12]), .c(multiplexer_4_out[12]), .sum(halfadder_1_sum[12]),
    .carry(fulladder_12_carry));
  FullAdder fulladder_13 (
    .a(fulladder_12_carry), .b(multiplexer_3_out[13]), .c(multiplexer_4_out[13]), .sum(halfadder_1_sum[13]),
    .carry(fulladder_13_carry));
  FullAdder fulladder_14 (
    .a(fulladder_13_carry), .b(multiplexer_3_out[14]), .c(multiplexer_4_out[14]), .sum(halfadder_1_sum[14]),
    .carry(fulladder_14_carry));
  FullAdder fulladder_15 (
    .a(fulladder_14_carry), .b(multiplexer_3_out[15]), .c(multiplexer_4_out[15]), .sum(halfadder_1_sum[15]));  // open: carry

  assign out[15] = ng;

  // Notes on the sheet:
  //   ADD16
endmodule

module HalfAdder (
  input  a,
  input  b,
  output sum,
  output carry
);

  xor Xor (sum, a, b);
  and And (carry, a, b);
endmodule

module FullAdder (
  input  a,
  input  b,
  input  c,
  output sum,
  output carry
);

  wire halfadder_1_carry, halfadder_1_sum, halfadder_2_carry;

  HalfAdder halfadder_1 (.a(a), .b(b), .sum(halfadder_1_sum), .carry(halfadder_1_carry));
  HalfAdder halfadder_2 (.a(halfadder_1_sum), .b(c), .sum(sum), .carry(halfadder_2_carry));
  HalfAdder halfadder_3 (.a(halfadder_1_carry), .b(halfadder_2_carry), .sum(carry));  // open: carry
endmodule

module Register (
  input  Load,
  input  [15:0] In,
  output [15:0] Out
);

  Bit bit_1 (.In(In[0]), .Load(Load), .Out(Out[0]));
  Bit bit_2 (.In(In[1]), .Load(Load), .Out(Out[1]));
  Bit bit_3 (.In(In[2]), .Load(Load), .Out(Out[2]));
  Bit bit_4 (.In(In[3]), .Load(Load), .Out(Out[3]));
  Bit bit_5 (.In(In[4]), .Load(Load), .Out(Out[4]));
  Bit bit_6 (.In(In[5]), .Load(Load), .Out(Out[5]));
  Bit bit_7 (.In(In[6]), .Load(Load), .Out(Out[6]));
  Bit bit_8 (.In(In[7]), .Load(Load), .Out(Out[7]));
  Bit bit_9 (.In(In[8]), .Load(Load), .Out(Out[8]));
  Bit bit_10 (.In(In[9]), .Load(Load), .Out(Out[9]));
  Bit bit_11 (.In(In[10]), .Load(Load), .Out(Out[10]));
  Bit bit_12 (.In(In[11]), .Load(Load), .Out(Out[11]));
  Bit bit_13 (.In(In[12]), .Load(Load), .Out(Out[12]));
  Bit bit_14 (.In(In[13]), .Load(Load), .Out(Out[13]));
  Bit bit_15 (.In(In[14]), .Load(Load), .Out(Out[14]));
  // Bit bit_16: pin names not known; wires that end beside it: Load, In[15], Load, Out[15]
endmodule

// RAM
module InstructionMemory (
  input  [15:0] in,
  input  [14:0] address,
  input  load,
  output [15:0] out
);

  wire a1_out, a2_out, b0_out, b1_out, b2_out, c1_out, c2_out, clock_1_out;
  wire [15:0] ram_1_data, ram_2_data, register_1_q;

  not b0 (b0_out, address[13]);
  and a2 (a2_out, load, a1_out);
  not a1 (a1_out, address[14]);
  and b2 (b2_out, load, b1_out);
  and b1 (b1_out, address[14], b0_out);
  and c2 (c2_out, load, c1_out);
  and c1 (c1_out, address[13], address[14]);
  Register_part #(.width(16)) register_1 (.D(in), .en(c2_out), .Q(register_1_q), .clk(clock_1_out));  // open: clr
  Clock clock_1 (.out(clock_1_out));
  RAM #(.addrWidth(14), .dataWidth(16), .bus("separate")) ram_1 (
    .addr(address[13:0]), .din(in), .data(ram_1_data), .sel(a2_out), .clk(clock_1_out));  // open: str, ld, clr
  Multiplexer #(.select(2), .width(16), .enable("false")) multiplexer_1 (
    .in0(ram_1_data), .in1(ram_1_data), .in2(ram_2_data), .in3(register_1_q), .out(out), .sel(address[14:13]));
  RAM #(.addrWidth(13), .dataWidth(16), .bus("separate")) ram_2 (
    .addr(address[12:0]), .din(in), .data(ram_2_data), .sel(b2_out), .clk(clock_1_out));  // open: str, ld, clr
endmodule

module PC (
  input  inc,
  input  [15:0] in,
  input  load,
  input  reset,
  output [15:0] out
);

  wire [15:0] adder_1_out, multiplexer_1_out, multiplexer_2_out, multiplexer_3_out;

  Multiplexer #(.width(16), .enable("false")) multiplexer_1 (
    .in0(out), .in1(adder_1_out), .out(multiplexer_1_out), .sel(inc));
  Multiplexer #(.width(16), .enable("false")) multiplexer_2 (
    .in0(multiplexer_1_out), .in1(in), .out(multiplexer_2_out), .sel(load));
  Multiplexer #(.width(16), .enable("false")) multiplexer_3 (
    .in0(multiplexer_2_out), .in1({16{1'b0}}), .out(multiplexer_3_out), .sel(reset));
  Adder #(.width(16)) adder_1 (.a(out), .b(16'h1), .out(adder_1_out));  // open: cin, cout
  Register \reg  (.In(multiplexer_3_out), .Load(1'b1), .Out(out));
endmodule

module CPU (
  input  [15:0] instruction,
  input  [15:0] inM,
  input  reset,
  output [14:0] addressM,
  output [15:0] outM,
  output writem,
  output [14:0] PC
);

  wire _0or_minus_out, AInst, ALUtoA, clock_1_out, inc, JEQ_out, JGT_out, JLE_2_out, JLE_out, JLT_out,
       JumpToA_out, load, loadA, loadD, ng, not_2_out, zr;
  wire [15:0] ALU, AMToALU, AMtoALU_t, AOut, DOut, toAReg;
  wire [15:15] or16_out, pc_1_p5;

  not not_1 (AInst, instruction[15]);
  and and_1 (ALUtoA, instruction[15], instruction[5]);
  or or_1 (loadA, AInst, ALUtoA);
  and and_2 (loadD, instruction[4], instruction[15]);
  or _0or_minus (_0or_minus_out, ng, zr);
  not not_2 (not_2_out, _0or_minus_out);
  and JLT (JLT_out, instruction[2], ng);
  and JEQ (JEQ_out, instruction[1], zr);
  and JGT (JGT_out, instruction[0], not_2_out);
  or JLE (JLE_out, JLT_out, JEQ_out);
  Multiplexer #(.width(16), .enable("false")) multiplexer_1 (.in0(instruction), .in1(ALU), .out(toAReg), .sel(ALUtoA));
  Register_part #(.width(16)) AREG (.D(toAReg), .en(loadA), .Q(AOut), .clk(clock_1_out));  // open: clr
  Register_part #(.width(16)) DREG (.D(ALU), .en(loadD), .Q(DOut), .clk(clock_1_out));  // open: clr
  Clock clock_1 (.out(clock_1_out));
  or JumpToA (JumpToA_out, JGT_out, JLE_2_out);
  or JLE_2 (JLE_2_out, JGT_out, JLE_out);
  Multiplexer #(.width(16), .enable("false")) multiplexer_2 (
    .in0(AOut), .in1(inM), .out(AMtoALU_t), .sel(instruction[12]));
  not not_3 (load, inc);
  and JGT_2 (inc, instruction[0], JumpToA_out);
  // PC pc_1: pin names not known; wires that end beside it: inc, load, reset, AOut, {pc_1_p5[15], PC}
  ALU alu_1 (
    .x(DOut), .y(AMToALU), .zx(instruction[11]), .zy(instruction[10]), .zx_2(instruction[9]),
    .zy_2(instruction[8]), .f(instruction[7]), .no(instruction[6]), .out(ALU), .zr(zr), .ng(ng));
  assign {or16_out[15], addressM} = AOut | {16{1'b0}};  // OR_Gate or16, 16 bits wide
  assign outM = ALU | {16{1'b0}};  // OR_Gate or16_2, 16 bits wide
  and JGT_3 (writem, instruction[15], instruction[3]);

  // Other names for the same wires on the sheet: i0 = instruction[0]; inst[15:0] = instruction; i1 = instruction[1];
  //   i2 = instruction[2]; i3 = instruction[3]; i4 = instruction[4]; i5 = instruction[5]; i6 = instruction[6];
  //   i7 = instruction[7]; i8 = instruction[8]; i9 = instruction[9]; i10 = instruction[10]; i11 = instruction[11];
  //   i12 = instruction[12]; i13 = instruction[13]; i14 = instruction[14]; CInst = instruction[15];
  //   i15 = instruction[15]

  // Notes on the sheet:
  //   positive
  //   PC DECODE
  //   ALU DECODE
  //   PC
  //   ALU
  //   OUTPUT HANDLING
endmodule

module wiredCPU (
  input  [15:0] instruction,
  input  [15:0] inM,
  input  reset,
  output [14:0] addressM,
  output [15:0] outM,
  output writem,
  output [14:0] PC
);

  wire _0or_minus_out, AInst, alu_1_ng, alu_1_zr, and_1_out, and_2_out, JEQ_out, JGT_2_out, JGT_out,
       JLE_2_out, JLE_out, JLT_out, JumpToA_out, not_2_out, not_3_out, or_1_out;
  wire [15:0] alu_1_out, AREG_q, DREG_q, multiplexer_1_out, multiplexer_2_out;
  wire [15:15] or16_out, pc_1_p5;

  not not_1 (AInst, instruction[15]);
  and and_1 (and_1_out, instruction[15], instruction[5]);
  Multiplexer #(.width(16), .enable("false")) multiplexer_1 (
    .in0(instruction), .in1(alu_1_out), .out(multiplexer_1_out), .sel(and_1_out));
  or or_1 (or_1_out, AInst, and_1_out);
  Register_part #(.width(16)) DREG (.D(alu_1_out), .en(and_2_out), .Q(DREG_q));  // open: clk, clr
  and and_2 (and_2_out, instruction[4], instruction[15]);
  Register_part #(.width(16)) AREG (.D(multiplexer_1_out), .en(or_1_out), .Q(AREG_q));  // open: clk, clr
  Multiplexer #(.width(16), .enable("false")) multiplexer_2 (
    .in0(AREG_q), .in1(inM), .out(multiplexer_2_out), .sel(instruction[12]));
  or _0or_minus (_0or_minus_out, alu_1_ng, alu_1_zr);
  not not_2 (not_2_out, _0or_minus_out);
  and JLT (JLT_out, instruction[2], alu_1_ng);
  and JEQ (JEQ_out, instruction[1], alu_1_zr);
  and JGT (JGT_out, instruction[0], not_2_out);
  or JLE (JLE_out, JLT_out, JEQ_out);
  ALU alu_1 (
    .x(DREG_q), .y(multiplexer_2_out), .zx(instruction[11]), .zy(instruction[10]), .zx_2(instruction[9]),
    .zy_2(instruction[8]), .f(instruction[7]), .no(instruction[6]), .out(alu_1_out), .zr(alu_1_zr),
    .ng(alu_1_ng));
  or JumpToA (JumpToA_out, JGT_out, JLE_2_out);
  or JLE_2 (JLE_2_out, JGT_out, JLE_out);
  not not_3 (not_3_out, JGT_2_out);
  and JGT_2 (JGT_2_out, instruction[0], JumpToA_out);
  assign {or16_out[15], addressM} = alu_1_out | {16{1'b0}};  // OR_Gate or16, 16 bits wide
  assign outM = AREG_q | {16{1'b0}};  // OR_Gate or16_2, 16 bits wide
  and JGT_3 (writem, instruction[15], instruction[3]);
  // PC pc_1: pin names not known; wires that end beside it: JGT_2_out, not_3_out, reset, AREG_q, {pc_1_p5[15], PC}

  // Other names for the same wires on the sheet: i0 = instruction[0]; inst[15:0] = instruction; i1 = instruction[1];
  //   i2 = instruction[2]; i3 = instruction[3]; i4 = instruction[4]; i5 = instruction[5]; i6 = instruction[6];
  //   i7 = instruction[7]; i8 = instruction[8]; i9 = instruction[9]; i10 = instruction[10]; i11 = instruction[11];
  //   i12 = instruction[12]; i13 = instruction[13]; i14 = instruction[14]; CInst = instruction[15];
  //   i15 = instruction[15]

  // Notes on the sheet:
  //   positive
  //   ALU
  //   PC DECODE
  //   OUTPUT HANDLING
  //   PC
endmodule

module Computer (
  input  in_1
);

  wire cpu_1_p4;
  wire [14:0] cpu_1_p6, cpu_1_p7;
  wire [15:0] cpu_1_p3, cpu_1_p5, rom_1_data;

  ROM #(.addrWidth(15), .dataWidth(16)) rom_1 (.addr(cpu_1_p7), .data(rom_1_data));  // open: sel
  // CPU cpu_1: pin names not known; wires that end beside it: in_1, rom_1_data, cpu_1_p3, cpu_1_p4, cpu_1_p5, cpu_1_p6, cpu_1_p7
  InstructionMemory instructionmemory_1 (.in(cpu_1_p5), .address(cpu_1_p6), .out(cpu_1_p3), .load(cpu_1_p4));

  // Notes on the sheet:
  //   contents of rom_1 (hex, n*v repeats v):
  //   677*0 fddf
endmodule
